// Logisim project PS2_keyboard Hincu Stefan si Babaisca Paul.circ as structural Verilog
module main (
  output Output_1,
  output [3:0] Output_bus_1,
  output [6:0] Output_bus_2
);

  wire clock_1_out, devider_1_clk_d, encoder_1_select0, encoder_1_select1;
  wire [3:0] ring_register_1_to_code;
  wire [4:0] keyboard_decoder_1_key1, keyboard_decoder_1_key2, keyboard_decoder_1_key3,
       keyboard_decoder_1_key4, mux_4_to_1_1_outputdigit;
  wire [7:0] ps2_receiver_1_data_received;

  Clock clock_1 (.out(clock_1_out));
  PS2_RECEIVER ps2_receiver_1 (
    .DATA_VALID(Output_1), .DATA_RECEIVED(ps2_receiver_1_data_received));  // open: CLK, PS2_CLK, PS2_DATA
  RING_REGISTER ring_register_1 (.CLK(devider_1_clk_d), .ANOZI(Output_bus_1), .TO_CODE(ring_register_1_to_code));
  DEVIDER devider_1 (.CLK(clock_1_out), .CLK_D(devider_1_clk_d));
  ENCODER encoder_1 (.DATA(ring_register_1_to_code), .SELECT0(encoder_1_select0), .SELECT1(encoder_1_select1));
  KEYBOARD_DECODER keyboard_decoder_1 (
    .DATA_RECEIVED(ps2_receiver_1_data_received), .KEY1(keyboard_decoder_1_key1),
    .KEY2(keyboard_decoder_1_key2), .KEY3(keyboard_decoder_1_key3), .KEY4(keyboard_decoder_1_key4));
  MUX_4_TO_1 mux_4_to_1_1 (
    .sel0(encoder_1_select0), .sel1(encoder_1_select1), .digit0(keyboard_decoder_1_key1),
    .digit1(keyboard_decoder_1_key2), .digit2(keyboard_decoder_1_key3), .digit3(keyboard_decoder_1_key4),
    .outputDigit(mux_4_to_1_1_outputdigit));
  SSDISPLAY ssdisplay_1 (.LETTER(mux_4_to_1_1_outputdigit), .catozi(Output_bus_2));
endmodule

// VHDL entity PS2_RECEIVER, as the project stores it:
--------------------------------------------------------------------------------
-- Project :
-- File    :
-- Autor   :
-- Date    :
--
--------------------------------------------------------------------------------
-- Description :
--
--------------------------------------------------------------------------------

LIBRARY ieee;
USE ieee.std_logic_1164.all;

ENTITY PS2_RECEIVER IS
  PORT (
  		CLK: in std_logic;
  		PS2_CLK: in std_logic;
  		PS2_DATA: in std_logic;
  		DATA_VALID: out std_logic;
  		DATA_RECEIVED: out std_logic_vector(7 downto 0)
       );
END PS2_RECEIVER;

--------------------------------------------------------------------------------
--Complete your VHDL description below
--------------------------------------------------------------------------------


ARCHITECTURE comportamentala OF PS2_RECEIVER IS
signal SHIFT_REGISTER: std_logic_vector (7 downto 0);
signal SHIFT_COUNT: integer range 0 to 11;
signal START_BIT_DETECTED: std_logic := '0';
BEGIN

	--- Numaram bitii care intra, trebuie sa intre 8 biti
	--- Detectam bitul de start si validam in functie de data_valid
	process(CLK)
	begin
		if(falling_edge(CLK)) then
			if PS2_CLK = '0' and PS2_CLK' event then
				if SHIFT_COUNT = 0 then
					if PS2_DATA = '0' then
						START_BIT_DETECTED <= '1';
						SHIFT_COUNT <= 1;
					end if;
				else
					SHIFT_REGISTER <= SHIFT_REGISTER(6 downto 0) & ps2_data;
					SHIFT_COUNT <= SHIFT_COUNT + 1;
					if SHIFT_COUNT = 9 then
						DATA_RECEIVED <= SHIFT_REGISTER;
						DATA_VALID <= '1';
						SHIFT_COUNT <= 0;
					end if;
				end if;
			else
				START_BIT_DETECTED <= '0';
			end if;
		end if;	
	end process;

	---Daca avem bit de start, atunci data_valid e 0 ceea ce inseamna ca nu bagam datele in received_data
	process(START_BIT_DETECTED)
	begin
		if START_BIT_DETECTED = '1' then
			DATA_VALID <= '0';
		end if;
	end process;
END comportamentala;

// VHDL entity KEYBOARD_DECODER, as the project stores it:
--------------------------------------------------------------------------------
-- Project :
-- File    :
-- Autor   :
-- Date    :
--
--------------------------------------------------------------------------------
-- Description :
--
--------------------------------------------------------------------------------

LIBRARY ieee;
USE ieee.std_logic_1164.all;

ENTITY KEYBOARD_DECODER IS
  PORT (
  		DATA_RECEIVED: in std_logic_vector (7 downto 0);
  		KEY1: out std_logic_vector(4 downto 0);
  		KEY2: out std_logic_vector(4 downto 0);
  		KEY3: out std_logic_vector(4 downto 0);
  		KEY4: out std_logic_vector(4 downto 0)
       );
END KEYBOARD_DECODER;

--------------------------------------------------------------------------------
--Complete your VHDL description below
--------------------------------------------------------------------------------

ARCHITECTURE comportamentala OF KEYBOARD_DECODER IS
signal temp1: std_logic_vector(4 downto 0);
signal temp2: std_logic_vector(4 downto 0);
signal temp3: std_logic_vector(4 downto 0);
signal temp4: std_logic_vector(4 downto 0);
BEGIN
	---proces pentru salvarea literelor sub forma de numere pe 5 biti 
	process(DATA_RECEIVED)
	begin
		temp4<=temp3;
		temp3<=temp2;
		temp2<=temp1;
		case (DATA_RECEIVED) is
			when "00011100" => temp1 <= "00001"; ---A;
			when "00110010" => temp1 <= "00010"; ---B;
			when "00100001" => temp1 <= "00011"; ---C;
			when "00100011" => temp1 <= "00100"; ---D;
			when "00100100" => temp1 <= "00101"; ---E;
			when "00101011" => temp1 <= "00110"; ---F;
			when "00110100" => temp1 <= "00111"; ---G;
			when "00110011" => temp1 <= "01000"; ---H;
			when "01000011" => temp1 <= "01001"; ---I;
			when "00111011" => temp1 <= "01010"; ---J;
			when "01000010" => temp1 <= "01011"; ---K;
			when "01001011" => temp1 <= "01100"; ---L;
			when "00111010" => temp1 <= "01101"; ---M;
			when "00110001" => temp1 <= "01110"; ---N;
			when "01000100" => temp1 <= "01111"; ---O;
			when "01001101" => temp1 <= "10000"; ---P;
			when "00010101" => temp1 <= "10001"; ---Q;
			when "00101101" => temp1 <= "10010"; ---R;
			when "00011011" => temp1 <= "10011"; ---S;
			when "00101100" => temp1 <= "10100"; ---T;
			when "00111100" => temp1 <= "10101"; ---U;
			when "00101010" => temp1 <= "10110"; ---V;
			when "00011101" => temp1 <= "10111"; ---W;
			when "00100010" => temp1 <= "11000"; ---X;
			when "00110101" => temp1 <= "11001"; ---Y;
			when "00011010" => temp1 <= "11010"; ---Z;
			when others => temp1 <= "00000";
			
		end case;
	end process;
KEY1<=temp1;
KEY2<=temp2;
KEY3<=temp3;
KEY4<=temp4;
		

END comportamentala;

// VHDL entity COUTER_FOR_DELAY, as the project stores it:
--------------------------------------------------------------------------------
-- Project :
-- File    :
-- Autor   :
-- Date    :
--
--------------------------------------------------------------------------------
-- Description :
--
--------------------------------------------------------------------------------

LIBRARY ieee;
USE ieee.std_logic_1164.all;
use ieee.std_logic_unsigned.all;

ENTITY COUTER_FOR_DELAY IS
  PORT (
  		CLK: in std_logic;
  		COUNT: out std_logic_vector (16 downto 0)
    );
END COUTER_FOR_DELAY;

--------------------------------------------------------------------------------
--Complete your VHDL description below
--------------------------------------------------------------------------------

ARCHITECTURE TypeArchitecture OF COUTER_FOR_DELAY IS

signal temp: std_logic_vector (16 downto 0);
BEGIN
process(CLK)
	begin 
		if (rising_edge(CLK)) then 
			if temp < "11111111111111111" then temp <= temp + "00000000000000001";
			else temp <= "00000000000000000";
			end if;
		end if;
end process;

COUNT <= temp;
END TypeArchitecture;

// VHDL entity TO_7_SEGMENT, as the project stores it:
--------------------------------------------------------------------------------
-- Project :
-- File    :
-- Autor   :
-- Date    :
--
--------------------------------------------------------------------------------
-- Description :
--
--------------------------------------------------------------------------------

LIBRARY ieee;
USE ieee.std_logic_1164.all;

ENTITY TO_7_SEGMENT IS
  PORT (
  		CLK: in std_logic;
  		LETTER: in std_logic_vector(4 downto 0);
  		SEGMENT1: out std_logic_vector (7 downto 0)
       );
END TO_7_SEGMENT;

--------------------------------------------------------------------------------
--Complete your VHDL description below
--------------------------------------------------------------------------------

ARCHITECTURE comportamentala OF TO_7_SEGMENT IS
signal temp1: std_logic_vector(7 downto 0);
BEGIN
	process(CLK)
	begin
		if(rising_edge(CLK)) then
			case LETTER is
				when "00001" => temp1 <="0001000";---A
				when "00010" => temp1 <="1111111";---B
				when "00011" => temp1 <="0110001";---C
				when "00100" => temp1 <="0000001";---D
				when "00101" => temp1 <="0110000";---E
				when "00110" => temp1 <="0111000";---F
				when "00111" => temp1 <="0100000";---G
				when "01000" => temp1 <="1001000";---H
				when "01001" => temp1 <="1001111";---I
				when "01010" => temp1 <="0000011";---J
				when "01011" => temp1 <="1001000";---K
				when "01100" => temp1 <="1110000";---L
				when "01101" => temp1 <="0001001";---M
				when "01110" => temp1 <="1101010";---N
				when "01111" => temp1 <="0000001";---O
				when "10000" => temp1 <="0011000";---P
				when "10001" => temp1 <="0000001";---Q
				when "10010" => temp1 <="0001000";---R
				when "10011" => temp1 <="0100100";---S
				when "10100" => temp1 <="0111001";---T
				when "10101" => temp1 <="1000001";---U
				when "10110" => temp1 <="1000001";---V
				when "10111" => temp1 <="1000001";---W
				when "11000" => temp1 <="1001000";---X
				when "11001" => temp1 <="1001100";---Y
				when "11010" => temp1 <="0010010";---Z
				when others => temp1 <="1111111";
			end case;
		end if;
	end process;
SEGMENT1 <=temp1;
END comportamentala;

// VHDL entity MUX_4_TO_1, as the project stores it:
--------------------------------------------------------------------------------
-- Project :
-- File    :
-- Autor   :
-- Date    :
--
--------------------------------------------------------------------------------
-- Description :
--
--------------------------------------------------------------------------------

LIBRARY ieee;
USE ieee.std_logic_1164.all;

ENTITY MUX_4_TO_1 IS
  PORT (
  sel0: in std_logic;
  sel1: in std_logic;

  digit0: in std_logic_vector (4 downto 0);
  digit1: in std_logic_vector (4 downto 0);
  digit2: in std_logic_vector (4 downto 0);
  digit3: in std_logic_vector (4 downto 0);

  outputDigit: out std_logic_vector (4 downto 0)
    );
END MUX_4_TO_1;

--------------------------------------------------------------------------------
--Complete your VHDL description below
--------------------------------------------------------------------------------

ARCHITECTURE TypeArchitecture OF mux_4_to_1 IS

BEGIN

outputDigit <= digit0 when (sel0 = '0' and sel1 = '0') else 
			digit1 when (sel0 = '0' and sel1 = '1') else 
			digit2 when (sel0 = '1' and sel1 = '0') else 
			digit3 when (sel0 = '1' and sel1 = '1') else 
			"00000";

END TypeArchitecture;

// VHDL entity SPLITER, as the project stores it:
--------------------------------------------------------------------------------
-- Project :
-- File    :
-- Autor   :
-- Date    :
--
--------------------------------------------------------------------------------
-- Description :
--
--------------------------------------------------------------------------------

LIBRARY ieee;
USE ieee.std_logic_1164.all;

ENTITY SPLITER IS
  PORT (
 		vector: in std_logic_vector(16 downto 0);
 		select0 : out std_logic;
 		select1 : out std_logic
       );
END SPLITER;

--------------------------------------------------------------------------------
--Complete your VHDL description below
--------------------------------------------------------------------------------

ARCHITECTURE TypeArchitecture OF SPLITER IS

BEGIN
	select0 <= vector(15);
	select1 <= vector(16);

END TypeArchitecture;

// VHDL entity RING_REGISTER, as the project stores it:
--------------------------------------------------------------------------------
-- Project :
-- File    :
-- Autor   :
-- Date    :
--
--------------------------------------------------------------------------------
-- Description :
--
--------------------------------------------------------------------------------

LIBRARY ieee;
USE ieee.std_logic_1164.all;

ENTITY RING_REGISTER IS
  PORT (
  		CLK: in std_logic;
  		ANOZI: out std_logic_vector(3 downto 0);
  		TO_CODE: out std_logic_vector(3 downto 0)
       );
END RING_REGISTER;

--------------------------------------------------------------------------------
--Complete your VHDL description below
--------------------------------------------------------------------------------

ARCHITECTURE TypeArchitecture OF RING_REGISTER IS
signal temp: std_logic_vector(3 downto 0):="0001";
BEGIN
	process(CLK)
	begin
		if(rising_edge(CLK)) then
			temp(3)<=temp(2);
			temp(2)<=temp(1);
			temp(1)<=temp(0);
			temp(0)<=temp(3);
		end if;
	end process;
ANOZi <=temp;
TO_CODE <=temp;
END TypeArchitecture;

// VHDL entity ENCODER, as the project stores it:
--------------------------------------------------------------------------------
-- Project :
-- File    :
-- Autor   :
-- Date    :
--
--------------------------------------------------------------------------------
-- Description :
--
--------------------------------------------------------------------------------

LIBRARY ieee;
USE ieee.std_logic_1164.all;

ENTITY ENCODER IS
  PORT (
 		DATA: in std_logic_vector(3 downto 0);
 		SELECT0: out std_logic;
 		SELECT1: out std_logic
       );
END ENCODER;

--------------------------------------------------------------------------------
--Complete your VHDL description below
--------------------------------------------------------------------------------

ARCHITECTURE TypeArchitecture OF ENCODER IS
signal temp: std_logic_vector(1 downto 0);
BEGIN
	process
	begin
	case DATA is
		when "0001" =>
			SELECT0 <='0';
			SELECT1 <='0';
		when "0010" => 
			SELECT0 <='1';
			SELECT1 <='0';
		when "0100" =>
			SELECT0 <='0';
			SELECT1 <='1';
		when "1000" =>
			SELECT0<='1';
			SELECT1<='1';
		when others =>
			SELECT0<='0';
			SELECT1<='0';
	end case;
	end process;

END TypeArchitecture;

// VHDL entity DEVIDER, as the project stores it:
--------------------------------------------------------------------------------
-- Project :
-- File    :
-- Autor   :
-- Date    :
--
--------------------------------------------------------------------------------
-- Description :
--
--------------------------------------------------------------------------------

LIBRARY ieee;
USE ieee.std_logic_1164.all;
use ieee.std_logic_unsigned.all;

ENTITY DEVIDER IS
  PORT (
  		CLK: in std_logic;
  		CLK_D: out std_logic
    );
END DEVIDER;

--------------------------------------------------------------------------------
--Complete your VHDL description below
--------------------------------------------------------------------------------

ARCHITECTURE TypeArchitecture OF DEVIDER IS

signal temp: std_logic_vector (16 downto 0);
BEGIN
process(CLK)
	begin 
		if (rising_edge(CLK)) then 
			temp <= temp+1;
			CLK_D <= temp(16);
			
		end if;
end process; 
END TypeArchitecture;

// VHDL entity SSDISPLAY, as the project stores it:
--------------------------------------------------------------------------------
-- Project :
-- File    :
-- Autor   :
-- Date    :
--
--------------------------------------------------------------------------------
-- Description :
--
--------------------------------------------------------------------------------

LIBRARY ieee;
USE ieee.std_logic_1164.all;

ENTITY SSDISPLAY IS
  PORT (
  		LETTER: in std_logic_vector (4 downto 0);
  		catozi: out std_logic_vector(6 downto 0)
       );
END SSDISPLAY;

--------------------------------------------------------------------------------
--Complete your VHDL description below
--------------------------------------------------------------------------------

ARCHITECTURE TypeArchitecture OF SSDISPLAY IS
signal temp: std_logic_vector(6 downto 0);
BEGIN
	process
	begin
		case (LETTER) is
				when "00001" => temp <="0001000";---A
				when "00010" => temp <="1111111";---B
				when "00011" => temp <="0110001";---C
				when "00100" => temp <="0000001";---D
				when "00101" => temp <="0110000";---E
				when "00110" => temp <="0111000";---F
				when "00111" => temp <="0100000";---G
				when "01000" => temp <="1001000";---H
				when "01001" => temp <="1001111";---I
				when "01010" => temp <="0000011";---J
				when "01011" => temp <="1001000";---K
				when "01100" => temp <="1110000";---L
				when "01101" => temp <="0001001";---M
				when "01110" => temp <="1101010";---N
				when "01111" => temp <="0000001";---O
				when "10000" => temp <="0011000";---P
				when "10001" => temp <="0000001";---Q
				when "10010" => temp <="0001000";---R
				when "10011" => temp <="0100100";---S
				when "10100" => temp <="0111001";---T
				when "10101" => temp <="1000001";---U
				when "10110" => temp <="1000001";---V
				when "10111" => temp <="1000001";---W
				when "11000" => temp <="1001000";---X
				when "11001" => temp <="1001100";---Y
				when "11010" => temp <="0010010";---Z
				when others => temp <="1111111";
			end case;
	end process;

END TypeArchitecture;
